// Logisim project Lucas_Neves_SI4N.circ as structural Verilog: 3 circuits, main circuit main
module main (
  input  in_1,
  input  in_2,
  input  [3:0] in_3,
  input  [3:0] in_4,
  input  in_5,
  output out_6,
  output out_7,
  output out_8,
  output [3:0] out_9
);

  ADD_1 add_1_1 (.A(in_1), .B(in_2), .Vem_1(in_5), .Soma(out_8), .Vai_1(out_6));
  ADD_4 add_4_1 (.in_2(in_3), .out_3(out_7), .in_1(in_4), .out_4(out_9));
endmodule

module ADD_1 (
  input  A,
  input  B,
  input  Vem_1,
  output Soma,
  output Vai_1
);

  wire and_1_out, and_2_out, and_3_out, and_4_out, and_5_out, and_6_out, and_7_out, not_1_out, not_2_out,
       not_3_out, not_4_out, not_5_out, not_6_out;

  not not_1 (not_1_out, A);
  not not_2 (not_2_out, B);
  not not_3 (not_3_out, A);
  not not_4 (not_4_out, Vem_1);
  not not_5 (not_5_out, B);
  not not_6 (not_6_out, Vem_1);
  and and_1 (and_1_out, B, Vem_1);
  and and_2 (and_2_out, A, Vem_1);
  and and_3 (and_3_out, A, B);
  and and_4 (and_4_out, not_1_out, not_2_out, Vem_1);
  and and_5 (and_5_out, not_3_out, B, not_4_out);
  and and_6 (and_6_out, A, not_5_out, not_6_out);
  and and_7 (and_7_out, A, B, Vem_1);
  or or_1 (Vai_1, and_1_out, and_2_out, and_3_out);
  or or_2 (Soma, and_4_out, and_5_out, and_6_out, and_7_out);
endmodule

module ADD_4 (
  input  [3:0] in_1,
  input  [3:0] in_2,
  output out_3,
  output [3:0] out_4
);

  wire add_1_2_vai_1, add_1_3_vai_1, add_1_4_vai_1;

  // Probe on in_2
  ADD_1 add_1_1 (.A(in_2[3]), .B(in_1[3]), .Vem_1(add_1_2_vai_1), .Soma(out_4[3]), .Vai_1(out_3));
  ADD_1 add_1_2 (.A(in_2[2]), .B(in_1[2]), .Vem_1(add_1_3_vai_1), .Soma(out_4[2]), .Vai_1(add_1_2_vai_1));
  ADD_1 add_1_3 (.A(in_2[1]), .B(in_1[1]), .Vem_1(add_1_4_vai_1), .Soma(out_4[1]), .Vai_1(add_1_3_vai_1));
  ADD_1 add_1_4 (.A(in_2[0]), .B(in_1[0]), .Vem_1(1'b0), .Soma(out_4[0]), .Vai_1(add_1_4_vai_1));
endmodule
